// Logisim project switch_debouncer_fsm_logic.circ as structural Verilog: 1 circuit, main circuit main
module main (
  output SW_DB,
  output CNT_RST
);

  wire and_1_out, and_2_out, and_3_out, and_4_out, and_5_out, and_6_out, and_7_out, and_8_out, and_9_out,
       and_10_out, and_11_out, button_1_out, clock_1_out, clock_2_out, comparator_1_eq, comparator_1_gt,
       comparator_1_lt, not_1_out, not_2_out, or_1_out, or_2_out, S0_q, S0_qn, S1_q, S1_qn;
  wire [3:0] adder_1_out, register_1_q;

  Button button_1 (.out(button_1_out));
  LED led_1 (.in(SW_DB));
  not not_1 (not_1_out, button_1_out);
  not not_2 (not_2_out, comparator_1_eq);
  Adder #(.width(4)) adder_1 (.a(register_1_q), .b(4'b0001), .out(adder_1_out));  // open: cin, cout
  Clock clock_1 (.out(clock_1_out));
  Register #(.width(4)) register_1 (.D(adder_1_out), .clk(clock_1_out), .Q(register_1_q), .clr(CNT_RST));  // open: en
  and and_1 (and_1_out, S1_q, not_1_out, not_2_out);
  and and_2 (and_2_out, S1_q, S0_qn, not_1_out);
  and and_3 (and_3_out, S1_qn, button_1_out, not_2_out);
  and and_4 (and_4_out, S1_qn, S0_qn, button_1_out);
  and and_5 (and_5_out, S1_q, S0_qn);
  and and_6 (and_6_out, S1_q, not_2_out);
  and and_7 (and_7_out, S1_qn, S0_q, comparator_1_eq);
  or or_1 (or_1_out, and_1_out, and_2_out, and_3_out, and_4_out);
  or or_2 (or_2_out, and_5_out, and_6_out, and_7_out);
  // NoConnect on comparator_1_gt
  Comparator #(.width(4)) comparator_1 (
    .a(register_1_q), .b(4'b0100), .gt(comparator_1_gt), .eq(comparator_1_eq), .lt(comparator_1_lt));
  // NoConnect on comparator_1_lt
  D_Flip_Flop S0 (.D(or_1_out), .clk(clock_2_out), .Q(S0_q), .Qn(S0_qn));  // open: preset, reset
  D_Flip_Flop S1 (.D(or_2_out), .clk(clock_2_out), .Q(S1_q), .Qn(S1_qn));  // open: preset, reset
  Clock clock_2 (.out(clock_2_out));
  and and_8 (and_8_out, S1_q, S0_qn);
  and and_9 (and_9_out, S1_q, S0_q);
  and and_10 (and_10_out, S1_qn, S0_qn);
  and and_11 (and_11_out, S1_q, S0_qn);
  or or_3 (SW_DB, and_8_out, and_9_out);
  or or_4 (CNT_RST, and_10_out, and_11_out);

  // Notes on the sheet:
  //   S0
  //   S1
endmodule
