// Logisim project switch_debouncer_fsm_ttl.circ as structural Verilog: 1 circuit, main circuit main
module main (
);

  wire button_1_out, CLK, CNT_DONE, CNT_RST, n7404_1_pin2, n7404_1_pin4, n7408_1_pin3, n7408_1_pin6,
       n7408_1_pin8, n7408_1_pin11, n7411_1_pin6, n7411_1_pin8, n7411_1_pin12, n7411_2_pin5, n7411_2_pin6,
       n7411_2_pin8, n7411_2_pin9, n7411_2_pin12, n7411_3_pin1, n7411_3_pin2, n7411_3_pin6, n7411_3_pin8,
       n7411_3_pin9, n7411_3_pin10, n7411_3_pin11, n7411_3_pin12, n7411_3_pin13, n7432_2_pin3, n7432_2_pin5,
       n7432_2_pin6, n7432_2_pin8, n7432_3_pin3, n7485_1_pin1, n7485_1_pin2, n7485_1_pin3, n7485_1_pin4,
       n7485_1_pin5, n7485_1_pin7, n7485_1_pin9, n7485_1_pin11, n7485_1_pin14, n74175_1_pin3, n74175_1_pin6,
       n74175_1_pin11, n74175_1_pin14, n74283_1_pin1, n74283_1_pin2, n74283_1_pin3, n74283_1_pin4,
       n74283_1_pin5, n74283_1_pin6, n74283_1_pin7, n74283_1_pin9, n74283_1_pin10, n74283_1_pin11,
       n74283_1_pin12, n74283_1_pin13, n74283_1_pin14, n74283_1_pin15, nS0, nS1, S0, S1, SW_DB;

  Button button_1 (.out(button_1_out));
  LED led_1 (.in(SW_DB));
  _7404 #(.ShowInternalStructure("true")) u_7404_1 (
    .pin1(button_1_out), .pin2(n7404_1_pin2), .pin3(CNT_DONE), .pin4(n7404_1_pin4));  // open: pin5, pin6, pin13, pin12, pin11, pin10, pin9, pin8
  _7408 #(.ShowInternalStructure("true")) u_7408_1 (
    .pin1(nS0), .pin2(nS1), .pin3(n7408_1_pin3), .pin4(nS0), .pin5(S1), .pin6(n7408_1_pin6), .pin13(nS0),
    .pin12(S1), .pin11(n7408_1_pin11), .pin10(S0), .pin9(S1), .pin8(n7408_1_pin8));
  _7411 #(.ShowInternalStructure("true")) u_7411_1 (
    .pin1(n7404_1_pin2), .pin2(n7404_1_pin4), .pin3(nS1), .pin4(button_1_out), .pin5(n7404_1_pin4),
    .pin6(n7411_1_pin6), .pin13(S1), .pin12(n7411_1_pin12), .pin11(S1), .pin10(nS0), .pin9(n7404_1_pin2),
    .pin8(n7411_1_pin8));
  _7432 #(.ShowInternalStructure("true")) u_7432_1 (
    .pin1(n7408_1_pin6), .pin2(n7408_1_pin3), .pin3(CNT_RST), .pin13(n7408_1_pin8), .pin12(n7408_1_pin11),
    .pin11(SW_DB));  // open: pin4, pin5, pin6, pin10, pin9, pin8
  _7411 #(.ShowInternalStructure("true")) u_7411_2 (
    .pin1(nS0), .pin2(button_1_out), .pin3(S1), .pin4(n7404_1_pin4), .pin5(n7411_2_pin5),
    .pin6(n7411_2_pin6), .pin13(nS1), .pin12(n7411_2_pin12), .pin11(S1), .pin10(nS0), .pin9(n7411_2_pin9),
    .pin8(n7411_2_pin8));
  // NoConnect on n7411_3_pin13
  // NoConnect on n7411_3_pin12
  // NoConnect on n7411_3_pin11
  _7411 #(.ShowInternalStructure("true")) u_7411_3 (
    .pin1(n7411_3_pin1), .pin2(n7411_3_pin2), .pin3(nS1), .pin4(S0), .pin5(CNT_DONE), .pin6(n7411_3_pin6),
    .pin13(n7411_3_pin13), .pin12(n7411_3_pin12), .pin11(n7411_3_pin11), .pin10(n7411_3_pin10),
    .pin9(n7411_3_pin9), .pin8(n7411_3_pin8));
  // NoConnect on n7411_3_pin1
  // NoConnect on n7411_3_pin2
  Clock clock_1 (.out(CLK));
  // NoConnect on n7411_3_pin10
  // NoConnect on n7411_3_pin9
  // NoConnect on n7411_3_pin8
  _7432 #(.ShowInternalStructure("true")) u_7432_2 (
    .pin1(n7411_1_pin6), .pin2(n7411_2_pin12), .pin3(n7432_2_pin3), .pin4(n7432_2_pin3), .pin5(n7432_2_pin5),
    .pin6(n7432_2_pin6), .pin13(n7411_1_pin12), .pin12(n7411_1_pin8), .pin11(n7432_2_pin5),
    .pin10(n7411_2_pin8), .pin9(n7411_2_pin6), .pin8(n7432_2_pin8));
  _74283 #(.ShowInternalStructure("true")) u_74283_1 (
    .pin1(n74283_1_pin1), .pin2(n74283_1_pin2), .pin3(n74283_1_pin3), .pin4(n74283_1_pin4),
    .pin5(n74283_1_pin5), .pin6(n74283_1_pin6), .pin7(n74283_1_pin7), .pin15(n74283_1_pin15),
    .pin14(n74283_1_pin14), .pin13(n74283_1_pin13), .pin12(n74283_1_pin12), .pin11(n74283_1_pin11),
    .pin10(n74283_1_pin10), .pin9(n74283_1_pin9));
  _7432 #(.ShowInternalStructure("true")) u_7432_3 (
    .pin1(n7432_2_pin8), .pin2(n7411_3_pin6), .pin3(n7432_3_pin3));  // open: pin4, pin5, pin6, pin13, pin12, pin11, pin10, pin9, pin8
  // NoConnect on n74283_1_pin9
  _7474 #(.ShowInternalStructure("true")) u_7474_1 (
    .pin2(n7432_2_pin6), .pin3(CLK), .pin5(S0), .pin6(nS0), .pin12(n7432_3_pin3), .pin11(CLK), .pin9(S1),
    .pin8(nS1));  // open: pin1, pin4, pin13, pin10
  _74175 #(.ShowInternalStructure("true")) u_74175_1 (
    .pin1(CNT_RST), .pin2(n74283_1_pin5), .pin3(n74175_1_pin3), .pin4(n74283_1_pin4), .pin5(n74283_1_pin1),
    .pin6(n74175_1_pin6), .pin7(n74283_1_pin3), .pin15(n74283_1_pin14), .pin14(n74175_1_pin14),
    .pin13(n74283_1_pin13), .pin12(n74283_1_pin10), .pin11(n74175_1_pin11), .pin10(n74283_1_pin12), .pin9(CLK));
  // NoConnect on n74175_1_pin14
  // NoConnect on n74175_1_pin11
  // NoConnect on n74175_1_pin3
  // NoConnect on n74175_1_pin6
  _7485 #(.ShowInternalStructure("true")) u_7485_1 (
    .pin1(n7485_1_pin1), .pin2(n7485_1_pin2), .pin3(n7485_1_pin3), .pin4(n7485_1_pin4), .pin5(n7485_1_pin5),
    .pin6(CNT_DONE), .pin7(n7485_1_pin7), .pin15(n74283_1_pin12), .pin14(n7485_1_pin14),
    .pin13(n74283_1_pin14), .pin12(n74283_1_pin3), .pin11(n7485_1_pin11), .pin10(n74283_1_pin5),
    .pin9(n7485_1_pin9));
  // NoConnect on n7485_1_pin5
  // NoConnect on n7485_1_pin7
  // also tied to GND on the sheet: {n74283_1_pin15, n74283_1_pin2, n74283_1_pin11, n74283_1_pin7, n7485_1_pin1, n7485_1_pin2, n7485_1_pin4, n7485_1_pin11, n7485_1_pin9}
  // also tied to VCC on the sheet: {n7411_2_pin5, n7411_2_pin9, n74283_1_pin6, n7485_1_pin14, n7485_1_pin3}
endmodule
